# Fritzing sketch Untitled Sketch (saved by Fritzing 0.9.3b)
breadboards: 1

parts:
  Composant1 = Arduino Uno (Rev3)
  T1 = LM35 Temperature Sensor [package="TO92 [THT]"]
  F1 = Small Fan, based on Fan - Ventilador [package=THT]
  VCC1 = Battery
  WeMos_D1_Mini_Relay_Shield_V1 = WeMos D1 Mini Relay Shield V2

nets:
  N1: Composant1.A0, T1.Vout
  N2: Composant1.D2, WeMos_D1_Mini_Relay_Shield_V1.D2
  N3: T1.+Vs, WeMos_D1_Mini_Relay_Shield_V1.5V
  N4: T1.GND, WeMos_D1_Mini_Relay_Shield_V1.G
  N5: F1.5V, WeMos_D1_Mini_Relay_Shield_V1.NO
  N6: F1.GND, VCC1.-
  N7: VCC1.+, WeMos_D1_Mini_Relay_Shield_V1.COM

custom parts:
  Small Fan, based on Fan - Ventilador: Small 2-pin fan, commonly used with single-board computers, 3d-printers, etc. This work is based on a much larger fan, as commonly found in desktop computers

// code stored in the sketch: Blink.ino
int sensor_temp = A0;
const int relayPin = D1;


void setup() {
  pinMode(relayPin, OUTPUT);
}


void loop() {
  int binary_value= analogRead(sensor_temp);
  float temp = binary_value * 0.4882; // 0.4882 correspond 1°C


  while(temp>=30){
    digitalWrite(relayPin, HIGH); // voltage HIGH
  }
}
