# Fritzing sketch l298n-arduino (saved by Fritzing 0.9.3b)
breadboards: 1

parts:
  L298N1 = L298N DC motor driver
  M1 = DC Motor
  Part1 = Arduino Uno (Rev3)
  U1 = LIPO-2000mAh [package=lipo-2000]
  U2 = LIPO-2000mAh [package=lipo-2000]
  R1 = Photocell (LDR) [package=THT]
  R2 = Resistor [tolerance=±5% resistance=100k package=THT]

nets:
  N1: L298N1.OUT3, M1.pin_2
  N2: L298N1.OUT4, M1.pin_1
  N3: L298N1.12V, U1.+
  N4: L298N1.GND, U2.-
  N5: L298N1.ENB, Part1.D5_PWM
  N6: L298N1.IN3, Part1.D7
  N7: L298N1.IN4, Part1.D6_PWM
  N8: Part1.A0, R1.pin_1, R2.Pin_0
  N9: Part1.5V, R1.pin_0
  N10: Part1.GND, R2.Pin_1
  N11: U1.-, U2.+

notes:
  2 x 3.7 V LiPo Batteries connected in series
  Right Motor
  L298N Motor Driver Board

custom parts:
  L298N DC motor driver: 2x DC motor driver with 78M05 positive voltage regulator (7..35 V) L298N: max 46 V, 2 A Set 5 V Enable jumper to enable 5 V regultor (needed for the L298N) and +5 V output at screw terminal or supply external +5 V at screw terminal Set ENA and/or ENB to +5 V to enable motor permanently or supply ENA and/or ENB with PWM signal IN1 and IN2 set rotation directory for motor A (OUT1/OUT2) IN2 and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

// code stored in the sketch: Untitled3.ino
int motor2pin1 = 7;
int motor2pin2 = 6;
int sensorpin = A0;


void setup() {
  pinMode(motor2pin1, OUTPUT);
  pinMode(motor2pin2, OUTPUT);
  pinMode(5, OUTPUT);
}


void loop() {


  int sensor=analogRead(sensorpin);


  if (sensor>300){
    analogWrite(5, 200);
    digitalWrite(motor2pin1, HIGH);
    digitalWrite(motor2pin2, LOW);
    delay(3000);
  }


  else{
  digitalWrite(motor2pin1, LOW);
  digitalWrite(motor2pin2, HIGH);
  delay(3000);
  }
 
}
